# Fritzing sketch Looping (saved by Fritzing 0.9.0b)

parts:
  IC2 = L293D [package=THT]
  9V = Screw terminal - 2 pins [package=THT]
  Part1 = Arduino Uno (Rev3) - ICSP  # not connected
  M1 = DC Motor
  R1 = Rotary Potentiometer (Large) [maximum_resistance=100kΩ package=THT]
  LED1 = LED - 5mm [color="Red (633nm)" package="5 mm [THT]"]
  LED2 = LED - 5mm [color="Red (633nm)" package="5 mm [THT]"]
  R2 = Resistor [package="2010 [SMD]"]
  R3 = Resistor [package="2010 [SMD]"]
  S3 = Toggle Switch [package=THT]
  S4 = Toggle Switch [package=THT]
  Part2 = Arduino Prototyping Shield
  IC3 = L293D [package=THT]

nets:
  N1: IC2.Enable_1, Part2.D9, Part2.N$16, Part2.N$165, IC3.Enable_1
  N2: IC2.In_1, Part2.D10, Part2.N$305, Part2.N$411, IC3.In_1
  N3: IC2.Out_1_(_Controlled_by_Enable_1_), M1.pin_2, Part2.N$269, Part2.N$313, IC3.Out_1_(_Controlled_by_Enable_1_)
  N4: IC2.0V, 9V.pin2, R1.leg1, LED1.anode, LED2.anode, S4.COM, Part2.GND, Part2.N$69, Part2.N$241, Part2.N$263, Part2.N$267, Part2.N$268, Part2.N$293, Part2.N$298, Part2.N$312, IC3.0V
  N5: IC2.Out_2_(_Controlled_by_Enable_1_), M1.pin_1, Part2.N$238, Part2.N$239, IC3.Out_2_(_Controlled_by_Enable_1_)
  N6: IC2.In_2, Part2.D11, Part2.N$233, Part2.N$236, IC3.In_2
  N7: IC2.+Vmotor, S3.L1, Part2.+9V, Part2.N$135, Part2.N$235, IC3.+Vmotor
  N8: IC2.Enable_2, Part2.N$259, IC3.Enable_2
  N9: IC2.In_3, Part2.N$261, IC3.In_3
  N10: IC2.Out_3_(_Controlled_by_Enable_2_), Part2.N$262, IC3.Out_3_(_Controlled_by_Enable_2_)
  N11: IC2.Out_4_(_Controlled_by_Enable_2_), Part2.N$297, IC3.Out_4_(_Controlled_by_Enable_2_)
  N12: IC2.In_4, Part2.N$299, IC3.In_4
  N13: IC2.+V, Part2.3.3V, Part2.N$319, Part2.N$377, IC3.+V
  N14: 9V.pin1, S3.COM, S3.L2
  N15: R1.wiper, Part2.A0
  N16: R1.leg2, Part2.+5V
  N17: LED1.cathode, R2.Pin_1, Part2.N$52, Part2.N$395
  N18: LED2.cathode, R3.Pin_1, Part2.N$39, Part2.N$43
  N19: R2.Pin_0, Part2.D4, Part2.N$423
  N20: R3.Pin_0, Part2.D3, Part2.N$424
  N21: S4.L1, Part2.D2
