# Fritzing sketch Orange Radio (saved by Fritzing 0.9.0b)

parts:
  Part1 = Adafruit MAX98306 Stereo 3.7W Class D Audio Amplifier [part_number="Adafruit #987"]
  SP1 = SPEAKER [package=pcb_mount_speaker]
  SP2 = SPEAKER [package=pcb_mount_speaker]
  Vin_Vout_GND = POT [package=pot_alpha_rv16af-20]
  Vin_Vout_GND1 = POT [package=pot_alpha_rv16af-20]
  5V = Screw terminal - 2 pins [package=THT]

nets:
  N1: Part1.LOUT-, SP2.+
  N2: Part1.LOUT+, SP2.-
  N3: Part1.ROUT+, SP1.-
  N4: Part1.ROUT-, SP1.+
  N5: Part1.15DB, Part1.GAIN1
  N6: Part1.IN_RIGHT+, Vin_Vout_GND1.S
  N7: Part1.IN_RIGHT-, Vin_Vout_GND1.A
  N8: Part1.IN_LEFT-, Vin_Vout_GND.A
  N9: Part1.IN_LEFT+, Vin_Vout_GND.S
  N10: Part1.GND, 5V.pin2
  N11: Part1.VDD, 5V.pin1

custom parts:
  Adafruit MAX98306 Stereo 3.7W Class D Audio Amplifier: This incredibly small stereo amplifier is surprisingly powerful - able to deliver 2 x 3.7W channels into 3 ohm impedance speakers. Inside the miniature chip is a class D controller, able to run from 2.7V-5.5VDC. Since the amp is a class D, its incredibly efficient (over 90% efficient when driving an 8Ω speaker at over a Watt) - making it perfect for portable and battery-powered projects. It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
