# Fritzing sketch Orange Radio2 (saved by Fritzing 0.9.0b)
breadboards: 1

parts:
  Raspberry_Pi1 = Raspberry Pi Zero
  5V = Screw terminal - 2 pins [package=THT]
  LED1 = smd LED [color="Red (633nm)" package="0603 [SMD]"]
  LED2 = smd LED [color="Red (633nm)" package="0603 [SMD]"]
  BUTTON1 = Square Pushbutton
  R1 = Resistor [package="2010 [SMD]"]
  R2 = Resistor [package="2010 [SMD]"]

nets:
  N1: Raspberry_Pi1.GIPO17, BUTTON1.leg1
  N2: Raspberry_Pi1.GIPO22, R2.Pin_0
  N3: Raspberry_Pi1.GND, 5V.pin2, LED1.cathode, LED2.cathode, BUTTON1.leg0
  N4: Raspberry_Pi1.GIPO14, R1.Pin_0
  N5: Raspberry_Pi1.5V, 5V.pin1
  N6: LED1.anode, R1.Pin_1
  N7: LED2.anode, R2.Pin_1

custom parts:
  Raspberry Pi Zero: The Raspberry Pi Zero is the latest single board computer to be released by the Raspberry Pi Foundation. It is the entry level model Raspberry Pi perfect for hobbyists, makers and industrial engineers looking to create solutions where small size and low power consumption are important. This is especially relevant for applications in the wearables space as well as up and coming applications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
