# Fritzing sketch Orange Radio2 (saved by Fritzing 0.9.3b)
breadboards: 1

parts:
  Raspberry_Pi1 = Raspberry Pi Zero
  LED1 = smd LED [color="Red (633nm)" package="0603 [SMD]"]
  LED2 = smd LED [color="Red (633nm)" package="0603 [SMD]"]
  BUTTON1 = Square Pushbutton
  R1 = Resistor [tolerance=±5% resistance=220 package="2010 [SMD]"]
  R2 = Resistor [tolerance=±5% resistance=220 package="2010 [SMD]"]
  R3 = Resistor [tolerance=±5% resistance=1k package=THT]
  BUTTON2 = Square Pushbutton
  R4 = Resistor [tolerance=±5% resistance=1k package=THT]

nets:
  N1: Raspberry_Pi1.3v3, R3.Pin_0, R4.Pin_0
  N2: Raspberry_Pi1.GIPO17, BUTTON1.leg0
  N3: Raspberry_Pi1.GIPO22, R2.Pin_0
  N4: Raspberry_Pi1.GIPO5, BUTTON2.leg0
  N5: Raspberry_Pi1.GND, LED1.cathode, LED2.cathode
  N6: Raspberry_Pi1.GIPO14, R1.Pin_0
  N7: LED1.anode, R1.Pin_1
  N8: LED2.anode, R2.Pin_1
  N9: BUTTON1.leg1, R3.Pin_1
  N10: BUTTON2.leg1, R4.Pin_1

custom parts:
  Raspberry Pi Zero: The Raspberry Pi Zero is the latest single board computer to be released by the Raspberry Pi Foundation. It is the entry level model Raspberry Pi perfect for hobbyists, makers and industrial engineers looking to create solutions where small size and low power consumption are important. This is especially relevant for applications in the wearables space as well as up and coming applications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
